// Digital circuit lab04.dig as structural Verilog
module lab04 (
  input  clk,
  input  rst,
  output [31:0] PC,
  output [5:0] opcode,
  output [4:0] src1__addr,
  output [31:0] src1__out,
  output [31:0] src2__addr,
  output [31:0] src2__out,
  output [31:0] dst__addr,
  output [31:0] dst__data
);

  wire ALUSrc, and_1_out, clk_t, mem_read, mem_to_reg, mem_write, reg_dst, reg_write, u_alu_3_zero,
       u_control_unit_branch;
  wire [1:0] alu_op;
  wire [3:0] alu_control;
  wire [10:0] cpumemory_d2;
  wire [31:0] alu_out, data_in, multiplexer_3_out, read_data, sex, u_alu_2_result, u_alu_result;

  gen_register #(.applicationType("IVERILOG"), .CodeFile("./gen_register.v")) u_gen_register (
    .clk(clk_t), .rst(rst), .write_en(clk_t), .data_in(data_in), .data_out(PC));
  alu #(.applicationType("IVERILOG"), .CodeFile("./alu.v")) u_alu (
    .alu_control(4'b0010), .A(data_in), .B(32'h4), .result(u_alu_result));  // open: zero
  RAMDualAccess #(.AddrBits(8), .isProgramMemory("true"), .Bits(32)) cpumemory (
    .str(mem_write), .C(clk_t), .ld(mem_read), .A1(alu_out[7:0]), .Din1(src2__out), .A2(PC[7:0]),
    .D1(read_data), .D2({opcode, src1__addr, src2__addr[4:0], src2__addr[4:0], cpumemory_d2}));
  Multiplexer #(.Bits(32)) multiplexer_1 (.sel(reg_dst), .in_0(src2__addr), .in_1(src2__addr), .out(dst__addr));
  Multiplexer #(.Bits(32)) multiplexer_2 (.sel(mem_to_reg), .in_0(alu_out), .in_1(read_data), .out(dst__data));
  control_unit #(.applicationType("IVERILOG"), .CodeFile("./control_unit.v")) u_control_unit (
    .instr_op(opcode), .reg_dst(reg_dst), .branch(u_control_unit_branch), .mem_read(mem_read),
    .mem_to_reg(mem_to_reg), .alu_op(alu_op), .mem_write(mem_write), .alu_src(ALUSrc), .reg_write(reg_write));
  cpu_registers #(.applicationType("IVERILOG"), .CodeFile("./cpu_registers.v")) u_cpu_registers (
    .clk(clk_t), .rst(rst), .write_en(reg_write), .src1_addr(src1__addr), .src2_addr(src2__addr[4:0]),
    .dst_addr(dst__addr[4:0]), .data_in(dst__data), .src1_out(src1__out), .src2_out(src2__out));
  alu_control #(.applicationType("IVERILOG"), .CodeFile("./alu_control.v")) u_alu_control (
    .alu_op(alu_op), .funct(cpumemory_d2[5:0]), .alu_control(alu_control));
  BitExtender #(.inputBits(16), .outputBits(32)) bitextender_1 (.in({src2__addr[4:0], cpumemory_d2}), .out(sex));
  alu #(.applicationType("IVERILOG"), .CodeFile("./alu.v")) u_alu_2 (
    .A(u_alu_result), .B({sex[29:0], 2'b00}), .result(u_alu_2_result));  // open: alu_control, zero
  Multiplexer #(.Bits(5)) multiplexer_3 (
    .sel(ALUSrc), .in_0(src2__out[4:0]), .in_1(sex[4:0]), .out(multiplexer_3_out[4:0]));
  alu #(.applicationType("IVERILOG"), .CodeFile("./alu.v")) u_alu_3 (
    .alu_control(alu_control), .A(src1__out), .B(multiplexer_3_out), .zero(u_alu_3_zero), .result(alu_out));
  and and_1 (and_1_out, u_control_unit_branch, u_alu_3_zero);
  Multiplexer #(.Bits(32)) multiplexer_4 (.sel(and_1_out), .in_0(u_alu_result), .in_1(u_alu_2_result), .out(data_in));
  // Pins of 5 and 32 bits meet at src2__addr
  // Pins of 5 and 32 bits meet at dst__addr
  // Pins of 5 and 32 bits meet at src2__out
  // Pins of 15 and 16 bits meet at {src2__addr[4:0], cpumemory_d2}
  // Pins of 5 and 32 bits meet at sex
  // Pins of 5 and 32 bits meet at multiplexer_3_out
  // Pins of 8 and 32 bits meet at alu_out

  // Other names for the same wires on the sheet: dst_addr[31:0] = dst__addr; src1_out[31:0] = src1__out;
  //   write_data[31:0] = src2__out

  // Notes on the sheet:
  //   Inputs
  //   PC
  //   Outputs for testing
endmodule
